# Fritzing sketch Lab06 Prelab Schematic (saved by Fritzing 0.9.0b)
breadboards: 1

parts:
  Launchpad1 = TI Launchpad MSP430G2
  DRIVER = H-Bridge [package=THT]
  REGULATOR = Voltage Regulator [package=to-220-alt]
  RIGHT_MOTOR = DC Motor
  LEFT_MOTOR = DC Motor
  V2 = DC Power [voltage=5]
  V3 = DC Power [voltage=5]
  V4 = DC Power [voltage=5]
  SENSOR = AD22100 - Voltage Output Temperature Sensor with Signal Conditioning [part_number=AD22100]

nets:
  N1: Launchpad1.p10, DRIVER.1A
  N2: Launchpad1.p9, DRIVER.2Y
  N3: Launchpad1.p8, DRIVER.1_2EN
  N4: Launchpad1.p11, REGULATOR.OUT, SENSOR.V+
  N5: Launchpad1.p14, DRIVER.3_4EN
  N6: Launchpad1.p15, DRIVER.4A
  N7: Launchpad1.p16, DRIVER.3A
  N8: Launchpad1.p17, SENSOR.Vo
  N9: DRIVER.1Y, LEFT_MOTOR.pin_1
  GND: DRIVER.GND1, DRIVER.GND2, DRIVER.GND3, DRIVER.GND4, REGULATOR.GND, SENSOR.GND
  N10: DRIVER.2A, LEFT_MOTOR.pin_2
  N11: DRIVER.VCC2, V2.V+
  N12: DRIVER.3Y, RIGHT_MOTOR.pin_2
  N13: DRIVER.4Y, RIGHT_MOTOR.pin_1
  5V: DRIVER.VCC1, REGULATOR.IN
  N14: V2.V-, V3.V+
  N15: V3.V-, V4.V+
